// Logisim project exercise1.circ as structural Verilog: 1 circuit, main circuit main
module main (
  input  [15:0] in_1,
  input  [15:0] in_2,
  input  [2:0] in_3,
  output [15:0] out_4
);

  wire [15:0] adder_1_out, AND_out, divider_1_out, multiplier_1_out, NAND_out, NOR_out, OR_out,
       subtractor_1_out;

  Adder #(.width(16)) adder_1 (.a(in_1), .b(in_2), .out(adder_1_out));  // open: cin, cout
  Subtractor #(.width(16)) subtractor_1 (.a(in_1), .b(in_2), .out(subtractor_1_out));  // open: bin, bout
  Multiplier #(.width(16)) multiplier_1 (.a(in_1), .b(in_2), .out(multiplier_1_out));  // open: cin, cout
  Divider #(.width(16)) divider_1 (.a(in_1), .b(in_2), .out(divider_1_out));  // open: upper, rem
  assign AND_out = in_1 & in_2;  // AND_Gate AND, 16 bits wide
  assign NAND_out = ~(in_1 & in_2);  // NAND_Gate NAND, 16 bits wide
  assign OR_out = in_1 | in_2;  // OR_Gate OR, 16 bits wide
  assign NOR_out = ~(in_1 | in_2);  // NOR_Gate NOR, 16 bits wide
  Multiplexer #(.select(3), .width(16), .enable("false")) multiplexer_1 (
    .in0(adder_1_out), .in1(subtractor_1_out), .in2(multiplier_1_out), .in3(divider_1_out), .in4(AND_out),
    .in5(NAND_out), .in6(OR_out), .in7(NOR_out), .out(out_4), .sel(in_3));
endmodule
